# Fritzing sketch war-of-dice (saved by Fritzing 0.9.3b)
breadboards: 1

parts:
  Part1 = Adafruit Feather 32u4 Adalogger [part_number="Adafruit #2795"]
  Part2 = Adafruit NeoPixel FeatherWing [part_number="Adafruit #2945"]
  S1 = Pushbutton [package="[SMD]"]
  S2 = Pushbutton [package="[SMD]"]

nets:
  GND: Part1.GND, Part2.GND, Part2.G, S1.Pin_1, S1.Pin_2, S2.Pin_1, S2.Pin_2
  N1: Part1.1, Part2.TX
  N2: Part1.0, Part2.RX
  N3: Part1.MISO, Part2.MISO
  N4: Part1.MOSI, Part2.MOSI
  N5: Part1.SCK, Part2.SCK
  N6: Part1.A5, Part2.F
  N7: Part1.A4, Part2.E
  N8: Part1.A3, Part2.D
  N9: Part1.A2, Part2.C
  N10: Part1.A1, Part2.B, S2.Pin_3, S2.Pin_4
  N11: Part1.A0, Part2.A, S1.Pin_3, S1.Pin_4
  N12: Part1.AREF, Part2.AREF
  N13: Part1.+3V3, Part2.3V
  N14: Part1.RST, Part2.RESET
  N15: Part1.VBAT, Part2.VBAT
  N16: Part1.EN, Part2.EN
  N17: Part1.VBUS, Part2.USB
  N18: Part1.13, Part2.N
  N19: Part1.12, Part2.M
  N20: Part1.11, Part2.L
  N21: Part1.10, Part2.K
  N22: Part1.9, Part2.J
  N23: Part1.6, Part2.I
  N24: Part1.5, Part2.H
  N25: Part1.3, Part2.SCL
  N26: Part1.2, Part2.SDA

custom parts:
  Adafruit Feather 32u4 Adalogger: This is the Adafruit Feather 32u4 Adalogger - our take on an 'all-in-one' datalogger (or data-reader) with built in USB and battery charging. Its an Adafruit Feather 32u4 with a microSD holder ready to rock! We have other boards in the Feather family, check'em out here At the Feather 32u4's heart is at ATmega32u4 clocked at 8 MHz and at 3.3V logic, a chip setup we've had tons of experience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
  Adafruit NeoPixel FeatherWing: Put on your sunglasses before staring into these 32 configurable eye-blistering RGB LEDs. Arranged in a 4x8 matrix, each pixel is individually addressable. Only one pin is required to control all the LEDs. On the bottom we have jumpers for the DIN line to any of the I/O pins on a Feather. You can cut the default jumper trace and use any pin you like To make it easy to start, the LEDs are by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
